// Logisim project 04_arithmetic_circuits.circ as structural Verilog: 23 circuits, main circuit HA_1bit
module HA_1bit (
  input  X0,
  input  X1,
  output Z,
  output Cout
);

  and and_1 (Cout, X1, X0);
  xor xor_1 (Z, X0, X1);
endmodule

module FAdd_1bit (
  input  Cin,
  input  A,
  input  B,
  output Z,
  output Cout
);

  wire and_1_out, and_2_out, xor_1_out;

  and and_1 (and_1_out, B, A);
  xor xor_1 (xor_1_out, A, B);
  or or_1 (Cout, and_1_out, and_2_out);
  and and_2 (and_2_out, xor_1_out, Cin);
  xor xor_2 (Z, Cin, xor_1_out);
endmodule

module FAdd_2bit (
  input  Cin,
  input  [1:0] A,
  input  [1:0] B,
  output [1:0] Z,
  output Cout
);

  wire fadd_1bit_1_cout;

  FAdd_1bit fadd_1bit_1 (.Cin(Cin), .A(A[0]), .B(B[0]), .Z(Z[0]), .Cout(fadd_1bit_1_cout));
  FAdd_1bit fadd_1bit_2 (.Cin(fadd_1bit_1_cout), .A(A[1]), .B(B[1]), .Z(Z[1]), .Cout(Cout));
endmodule

module FAdd_4bit (
  input  Cin,
  input  [3:0] A,
  input  [3:0] B,
  output [3:0] Z,
  output Cout
);

  wire fadd_2bit_1_cout;

  FAdd_2bit fadd_2bit_1 (.Cin(Cin), .A(A[1:0]), .B(B[1:0]), .Z(Z[1:0]), .Cout(fadd_2bit_1_cout));
  FAdd_2bit fadd_2bit_2 (.Cin(fadd_2bit_1_cout), .A(A[3:2]), .B(B[3:2]), .Z(Z[3:2]), .Cout(Cout));
endmodule

module FAdd_8bit (
  input  Cin,
  input  [7:0] A,
  input  [7:0] B,
  output [7:0] Z,
  output Cout
);

  wire fadd_4bit_1_cout;

  FAdd_4bit fadd_4bit_1 (.Cin(Cin), .A(A[3:0]), .B(B[3:0]), .Z(Z[3:0]), .Cout(fadd_4bit_1_cout));
  FAdd_4bit fadd_4bit_2 (.Cin(fadd_4bit_1_cout), .A(A[7:4]), .B(B[7:4]), .Z(Z[7:4]), .Cout(Cout));
endmodule

module FSub_1bit (
  input  A,
  input  B,
  output Z,
  output Cout
);

  wire not_1_out;

  not not_1 (not_1_out, B);
  FAdd_1bit fadd_1bit_1 (.Cin(1'b1), .A(A), .B(not_1_out), .Z(Z), .Cout(Cout));
endmodule

module FSub_2bit (
  input  [1:0] A,
  input  [1:0] B,
  output [1:0] Z,
  output Cout
);

  wire [1:0] not_1_out;

  assign not_1_out = ~B;  // NOT_Gate not_1, 2 bits wide
  FAdd_2bit fadd_2bit_1 (.Cin(1'b1), .A(A), .B(not_1_out), .Z(Z), .Cout(Cout));
endmodule

module FSub_4bit (
  input  [3:0] A,
  input  [3:0] B,
  output [3:0] Z,
  output Cout
);

  wire [3:0] not_1_out;

  assign not_1_out = ~B;  // NOT_Gate not_1, 4 bits wide
  FAdd_4bit fadd_4bit_1 (.Cin(1'b1), .A(A), .B(not_1_out), .Z(Z), .Cout(Cout));
endmodule

module FSub_8bit (
  input  [7:0] A,
  input  [7:0] B,
  output [7:0] Z,
  output Cout
);

  wire [7:0] not_1_out;

  assign not_1_out = ~B;  // NOT_Gate not_1, 8 bits wide
  FAdd_8bit fadd_8bit_1 (.Cin(1'b1), .A(A), .B(not_1_out), .Z(Z), .Cout(Cout));
endmodule

module FAS_1bit (
  input  Cin,
  input  A,
  input  B,
  input  S,
  output Z,
  output Cout
);

  wire or_1_out, xor_1_out;

  or or_1 (or_1_out, Cin, S);
  xor xor_1 (xor_1_out, B, S);
  FAdd_1bit fadd_1bit_1 (.Cin(or_1_out), .A(A), .B(xor_1_out), .Z(Z), .Cout(Cout));

  // Notes on the sheet:
  //   Cin always on in case of Sub (S=1)
  //   Add: S=0, Sub: S=1
endmodule

module FAS_2bit (
  input  Cin,
  input  [1:0] A,
  input  [1:0] B,
  input  S,
  output [1:0] Z,
  output Cout
);

  wire fas_1bit_1_cout;

  FAS_1bit fas_1bit_1 (.Cin(Cin), .A(A[0]), .B(B[0]), .S(S), .Z(Z[0]), .Cout(fas_1bit_1_cout));
  FAS_1bit fas_1bit_2 (.Cin(fas_1bit_1_cout), .A(A[1]), .B(B[1]), .S(S), .Z(Z[1]), .Cout(Cout));

  // Notes on the sheet:
  //   Add: S=0, Sub: S=1
endmodule

module FAS_4bit (
  input  Cin,
  input  [3:0] A,
  input  [3:0] B,
  input  S,
  output [3:0] Z,
  output Cout
);

  wire fas_2bit_1_cout;

  FAS_2bit fas_2bit_1 (.Cin(Cin), .A(A[1:0]), .B(B[1:0]), .S(S), .Z(Z[1:0]), .Cout(fas_2bit_1_cout));
  FAS_2bit fas_2bit_2 (.Cin(fas_2bit_1_cout), .A(A[3:2]), .B(B[3:2]), .S(S), .Z(Z[3:2]), .Cout(Cout));

  // Notes on the sheet:
  //   Add: S=0, Sub: S=1
endmodule

module FAS_8bit (
  input  Cin,
  input  [7:0] A,
  input  [7:0] B,
  input  S,
  output [7:0] Z,
  output Cout
);

  wire fas_4bit_1_cout;

  FAS_4bit fas_4bit_1 (.Cin(Cin), .A(A[3:0]), .B(B[3:0]), .S(S), .Z(Z[3:0]), .Cout(fas_4bit_1_cout));
  FAS_4bit fas_4bit_2 (.Cin(fas_4bit_1_cout), .A(A[7:4]), .B(B[7:4]), .S(S), .Z(Z[7:4]), .Cout(Cout));

  // Notes on the sheet:
  //   Add: S=0, Sub: S=1
endmodule

module FAS_nB_1bit (
  input  Cin,
  input  A,
  input  B,
  input  nB,
  output Z,
  output Cout
);

  wire xor_1_out;

  xor xor_1 (xor_1_out, B, nB);
  FAdd_1bit fadd_1bit_1 (.Cin(Cin), .A(A), .B(xor_1_out), .Z(Z), .Cout(Cout));

  // Notes on the sheet:
  //   Add: Cin=0, Sub: Cin=1
endmodule

module FAS_nB_2bit (
  input  Cin,
  input  [1:0] A,
  input  [1:0] B,
  output [1:0] Z,
  output Cout
);

  wire fas_nb_1bit_1_cout;

  FAS_nB_1bit fas_nb_1bit_1 (.Cin(Cin), .A(A[0]), .B(B[0]), .nB(Cin), .Z(Z[0]), .Cout(fas_nb_1bit_1_cout));
  FAS_nB_1bit fas_nb_1bit_2 (.Cin(fas_nb_1bit_1_cout), .A(A[1]), .B(B[1]), .nB(Cin), .Z(Z[1]), .Cout(Cout));

  // Notes on the sheet:
  //   Add: Cin=0, Sub: Cin=1
endmodule

module FAS_nB_4bit (
  input  Cin,
  input  [3:0] A,
  input  [3:0] B,
  output [3:0] Z,
  output Cout
);

  wire fas_nb_2bit_1_cout;

  FAS_nB_2bit fas_nb_2bit_1 (.Cin(Cin), .A(A[1:0]), .B(B[1:0]), .Z(Z[1:0]), .Cout(fas_nb_2bit_1_cout));
  FAS_nB_2bit fas_nb_2bit_2 (.Cin(fas_nb_2bit_1_cout), .A(A[3:2]), .B(B[3:2]), .Z(Z[3:2]), .Cout(Cout));

  // Notes on the sheet:
  //   Add: Cin=0, Sub: Cin=1
endmodule

module FAS_Cin_8bit (
  input  Cin,
  input  [7:0] A,
  input  [7:0] B,
  output [7:0] Z,
  output Cout
);

  wire fas_nb_4bit_1_cout;

  FAS_nB_4bit fas_nb_4bit_1 (.Cin(Cin), .A(A[3:0]), .B(B[3:0]), .Z(Z[3:0]), .Cout(fas_nb_4bit_1_cout));
  FAS_nB_4bit fas_nb_4bit_2 (.Cin(fas_nb_4bit_1_cout), .A(A[7:4]), .B(B[7:4]), .Z(Z[7:4]), .Cout(Cout));

  // Notes on the sheet:
  //   Add: Cin=0, Sub: Cin=1
endmodule

module ALU_v1_1bit (
  input  Cin,
  input  A,
  input  B,
  input  [1:0] S,
  output Result,
  output Cout
);

  wire and_1_out, fadd_1bit_1_cout, fadd_1bit_1_z, fsub_1bit_1_cout, fsub_1bit_1_z, or_1_out, undriven;

  and and_1 (and_1_out, A, B);
  or or_1 (or_1_out, A, B);
  FAdd_1bit fadd_1bit_1 (.Cin(Cin), .A(A), .B(B), .Z(fadd_1bit_1_z), .Cout(fadd_1bit_1_cout));
  FSub_1bit fsub_1bit_1 (.A(A), .B(B), .Z(fsub_1bit_1_z), .Cout(fsub_1bit_1_cout));
  MUX_4to1_1bit mux_4to1_1bit_1 (
    .X0(and_1_out), .X1(or_1_out), .X2(fadd_1bit_1_z), .X3(fsub_1bit_1_z), .S(S), .O(Result));
  MUX_4to1_1bit mux_4to1_1bit_2 (
    .X0(undriven), .X1(undriven), .X2(fadd_1bit_1_cout), .X3(fsub_1bit_1_cout), .S(S), .O(Cout));

  // Notes on the sheet:
  //   And: S=00, Or: S=01, Add: S=10, Sub: S=11
endmodule

module ALU_v2_F_1bit (
  input  Cin,
  input  A,
  input  B,
  input  [1:0] S,
  output Result,
  output Zero,
  output Overflow,
  output Cout,
  output Negative
);

  wire and_1_out, fas_1bit_1_z, IsSub_out, not_2_out, or_1_out, or_2_out;

  and and_1 (and_1_out, A, B);
  or or_1 (or_1_out, A, B);
  FAS_1bit fas_1bit_1 (.Cin(Cin), .A(A), .B(B), .S(IsSub_out), .Z(fas_1bit_1_z), .Cout(Cout));
  and IsSub (IsSub_out, S[1], S[0]);
  MUX_3to1_1bit mux_3to1_1bit_1 (.X0(and_1_out), .X1(or_1_out), .X2(fas_1bit_1_z), .S(S), .O(Result));
  not not_1 (Zero, Result);
  or or_2 (or_2_out, Cin, IsSub_out);
  not not_2 (not_2_out, Cout);
  xor xor_1 (Overflow, or_2_out, Cout);
  and and_2 (Negative, not_2_out, IsSub_out);

  // Notes on the sheet:
  //   And: S=00, Or: S=01, Add: S=10, Sub: S=11
endmodule

module ALU_v2_nF_1bit (
  input  Cin,
  input  A,
  input  B,
  input  [1:0] S,
  output Result,
  output Zero,
  output Overflow,
  output Cout
);

  wire and_1_out, fas_1bit_1_z, IsSub_out, or_1_out, or_2_out;

  and and_1 (and_1_out, A, B);
  or or_1 (or_1_out, A, B);
  FAS_1bit fas_1bit_1 (.Cin(Cin), .A(A), .B(B), .S(IsSub_out), .Z(fas_1bit_1_z), .Cout(Cout));
  and IsSub (IsSub_out, S[1], S[0]);
  MUX_3to1_1bit mux_3to1_1bit_1 (.X0(and_1_out), .X1(or_1_out), .X2(fas_1bit_1_z), .S(S), .O(Result));
  not not_1 (Zero, Result);
  or or_2 (or_2_out, Cin, IsSub_out);
  xor xor_1 (Overflow, or_2_out, Cout);

  // Notes on the sheet:
  //   And: S=00, Or: S=01, Add: S=10, Sub: S=11
endmodule

module ALU_Prof_1bit (
  input  nB,
  input  Cin,
  input  A,
  input  B,
  input  [1:0] S,
  output Result,
  output Overflow,
  output Cout
);

  wire and_1_out, fas_nb_1bit_1_z, or_1_out;

  and and_1 (and_1_out, A, B);
  or or_1 (or_1_out, A, B);
  FAS_nB_1bit fas_nb_1bit_1 (.Cin(Cin), .A(A), .B(B), .nB(nB), .Z(fas_nb_1bit_1_z), .Cout(Cout));
  MUX_3to1_1bit mux_3to1_1bit_1 (.X0(and_1_out), .X1(or_1_out), .X2(fas_nb_1bit_1_z), .S(S), .O(Result));
  xor xor_1 (Overflow, Cin, Cout);

  // Notes on the sheet:
  //   And: S=00, Or: S=01, Add: S=10, Sub: S=11
endmodule

module ALU_Optimized_1bit (
  input  [1:0] op,
  input  Cin,
  input  A,
  input  B,
  output result,
  output over,
  output Cout
);

  wire and_1_out, and_2_out, AND_OP_out, FA_OP_0_out, FA_OP_1_out, or_1_out, OR_OP_out, xor_1_out;

  and and_1 (and_1_out, op[1], op[0]);
  or or_1 (or_1_out, and_1_out, Cin);
  xor xor_1 (xor_1_out, B, and_1_out);
  and AND_OP (AND_OP_out, A, xor_1_out);
  or OR_OP (OR_OP_out, A, xor_1_out);
  xor FA_OP_0 (FA_OP_0_out, A, xor_1_out);
  xor FA_OP_1 (FA_OP_1_out, or_1_out, FA_OP_0_out);
  and and_2 (and_2_out, or_1_out, FA_OP_0_out);
  Multiplexer #(.select(2)) multiplexer_1 (
    .in0(AND_OP_out), .in1(OR_OP_out), .in2(FA_OP_1_out), .in3(FA_OP_1_out), .out(result), .sel(op));
  or or_2 (Cout, and_2_out, AND_OP_out);
  xor xor_2 (over, or_1_out, Cout);

  // Notes on the sheet:
  //   AND: op=00, OR: op=01, ADD: op=10, SUB: op=11
endmodule

module ALU_Optimized_8bit (
  input  [1:0] op,
  input  [7:0] A,
  input  [7:0] B,
  input  Cin,
  output [7:0] result,
  output zero,
  output neg,
  output over,
  output Cout
);

  wire alu_optimized_1bit_1_cout, alu_optimized_1bit_2_cout, alu_optimized_1bit_3_cout,
       alu_optimized_1bit_4_cout, alu_optimized_1bit_5_cout, alu_optimized_1bit_6_cout,
       alu_optimized_1bit_7_cout;

  ALU_Optimized_1bit alu_optimized_1bit_1 (
    .op(op), .Cin(Cin), .A(A[0]), .B(B[0]), .result(result[0]), .Cout(alu_optimized_1bit_1_cout));  // open: over
  ALU_Optimized_1bit alu_optimized_1bit_2 (
    .op(op), .Cin(alu_optimized_1bit_1_cout), .A(A[1]), .B(B[1]), .result(result[1]),
    .Cout(alu_optimized_1bit_2_cout));  // open: over
  ALU_Optimized_1bit alu_optimized_1bit_3 (
    .op(op), .Cin(alu_optimized_1bit_2_cout), .A(A[2]), .B(B[2]), .result(result[2]),
    .Cout(alu_optimized_1bit_3_cout));  // open: over
  ALU_Optimized_1bit alu_optimized_1bit_4 (
    .op(op), .Cin(alu_optimized_1bit_3_cout), .A(A[3]), .B(B[3]), .result(result[3]),
    .Cout(alu_optimized_1bit_4_cout));  // open: over
  ALU_Optimized_1bit alu_optimized_1bit_5 (
    .op(op), .Cin(alu_optimized_1bit_4_cout), .A(A[4]), .B(B[4]), .result(result[4]),
    .Cout(alu_optimized_1bit_5_cout));  // open: over
  ALU_Optimized_1bit alu_optimized_1bit_6 (
    .op(op), .Cin(alu_optimized_1bit_5_cout), .A(A[5]), .B(B[5]), .result(result[5]),
    .Cout(alu_optimized_1bit_6_cout));  // open: over
  ALU_Optimized_1bit alu_optimized_1bit_7 (
    .op(op), .Cin(alu_optimized_1bit_6_cout), .A(A[6]), .B(B[6]), .result(result[6]),
    .Cout(alu_optimized_1bit_7_cout));  // open: over
  ALU_Optimized_1bit alu_optimized_1bit_8 (
    .op(op), .Cin(alu_optimized_1bit_7_cout), .A(A[7]), .B(B[7]), .result(neg), .over(over), .Cout(Cout));
  nor nor_1 (zero, result[0], result[1], result[2], result[3], result[4], result[5], result[6], neg);

  assign result[7] = neg;
endmodule
