// Logisim project 06_arithmetic_and_registers.circ as structural Verilog: 8 circuits, main circuit ALU_1bit
module LATCH_SR (
  input  reset,
  input  R,
  input  S,
  input  clock,
  output Q,
  output nQ
);

  wire and_1_out, and_2_out;

  and and_1 (and_1_out, R, clock);
  and and_2 (and_2_out, S, clock);
  nor nor_1 (Q, and_1_out, reset, nQ);
  nor nor_2 (nQ, Q, and_2_out);
endmodule

module LATCH_D (
  input  D,
  input  clock,
  input  reset,
  output Q,
  output nQ
);

  wire not_1_out;

  not not_1 (not_1_out, D);
  LATCH_SR latch_sr_1 (.R(D), .S(not_1_out), .clock(clock), .reset(reset), .Q(Q), .nQ(nQ));
endmodule

module FLIPFLOP_D (
  input  D,
  input  clock,
  input  reset,
  output Q,
  output nQ
);

  wire latch_d_1_q, not_1_out;

  LATCH_D latch_d_1 (.D(D), .clock(not_1_out), .reset(reset), .Q(latch_d_1_q));  // open: nQ
  not not_1 (not_1_out, clock);
  LATCH_D latch_d_2 (.D(latch_d_1_q), .clock(clock), .reset(reset), .Q(Q), .nQ(nQ));
endmodule

module REGISTER_1bit (
  input  D,
  input  enable,
  input  clock,
  input  reset,
  output Q,
  output nQ
);

  wire multiplexer_1_out;

  Multiplexer multiplexer_1 (.in0(Q), .in1(D), .out(multiplexer_1_out), .sel(enable));
  FLIPFLOP_D flipflop_d_1 (.D(multiplexer_1_out), .clock(clock), .reset(reset), .Q(Q), .nQ(nQ));
endmodule

module REGISTER_8bit (
  input  [7:0] InWord,
  input  IE,
  input  clock,
  input  reset,
  input  OE,
  output [7:0] OutWord
);

  wire register_1bit_1_q, register_1bit_2_q, register_1bit_3_q, register_1bit_4_q, register_1bit_5_q,
       register_1bit_6_q, register_1bit_7_q, register_1bit_8_q;

  REGISTER_1bit register_1bit_1 (
    .D(InWord[7]), .enable(IE), .clock(clock), .reset(reset), .Q(register_1bit_1_q));  // open: nQ
  assign OutWord[7] = OE ? register_1bit_1_q : 1'bz;  // Controlled_Buffer controlled_buffer_1
  REGISTER_1bit register_1bit_2 (
    .D(InWord[6]), .enable(IE), .clock(clock), .reset(reset), .Q(register_1bit_2_q));  // open: nQ
  assign OutWord[6] = OE ? register_1bit_2_q : 1'bz;  // Controlled_Buffer controlled_buffer_2
  REGISTER_1bit register_1bit_3 (
    .D(InWord[5]), .enable(IE), .clock(clock), .reset(reset), .Q(register_1bit_3_q));  // open: nQ
  assign OutWord[5] = OE ? register_1bit_3_q : 1'bz;  // Controlled_Buffer controlled_buffer_3
  REGISTER_1bit register_1bit_4 (
    .D(InWord[4]), .enable(IE), .clock(clock), .reset(reset), .Q(register_1bit_4_q));  // open: nQ
  assign OutWord[4] = OE ? register_1bit_4_q : 1'bz;  // Controlled_Buffer controlled_buffer_4
  REGISTER_1bit register_1bit_5 (
    .D(InWord[3]), .enable(IE), .clock(clock), .reset(reset), .Q(register_1bit_5_q));  // open: nQ
  assign OutWord[3] = OE ? register_1bit_5_q : 1'bz;  // Controlled_Buffer controlled_buffer_5
  REGISTER_1bit register_1bit_6 (
    .D(InWord[2]), .enable(IE), .clock(clock), .reset(reset), .Q(register_1bit_6_q));  // open: nQ
  assign OutWord[2] = OE ? register_1bit_6_q : 1'bz;  // Controlled_Buffer controlled_buffer_6
  REGISTER_1bit register_1bit_7 (
    .D(InWord[1]), .enable(IE), .clock(clock), .reset(reset), .Q(register_1bit_7_q));  // open: nQ
  assign OutWord[1] = OE ? register_1bit_7_q : 1'bz;  // Controlled_Buffer controlled_buffer_7
  REGISTER_1bit register_1bit_8 (
    .D(InWord[0]), .enable(IE), .clock(clock), .reset(reset), .Q(register_1bit_8_q));  // open: nQ
  assign OutWord[0] = OE ? register_1bit_8_q : 1'bz;  // Controlled_Buffer controlled_buffer_8
endmodule

module MEMORY_8x8bit (
  input  [2:0] sel_I0,
  input  [7:0] I0,
  input  [2:0] sel_O0,
  input  [2:0] sel_O1,
  input  enable,
  input  write,
  input  reset,
  input  clock,
  input  clear,
  output [7:0] O0,
  output [7:0] O1
);

  wire and_1_out, decoder_1_out0, decoder_1_out1, or_1_out, or_2_out, or_3_out, or_4_out, or_5_out, or_6_out,
       or_7_out, or_8_out;
  wire [1:0] demultiplexer_1_out0, demultiplexer_1_out1, demultiplexer_1_out2, demultiplexer_1_out3,
       demultiplexer_1_out4, demultiplexer_1_out5, demultiplexer_1_out6, demultiplexer_1_out7;
  wire [7:0] register_8bit_1_outword, register_8bit_2_outword, register_8bit_3_outword,
       register_8bit_4_outword, register_8bit_5_outword, register_8bit_6_outword, register_8bit_7_outword,
       register_8bit_8_outword;

  Demultiplexer #(.enable("true"), .select(3), .width(2)) demultiplexer_1 (
    .out0(demultiplexer_1_out0), .out1(demultiplexer_1_out1), .out2(demultiplexer_1_out2),
    .out3(demultiplexer_1_out3), .out4(demultiplexer_1_out4), .out5(demultiplexer_1_out5),
    .out6(demultiplexer_1_out6), .out7(demultiplexer_1_out7), .in({clear, clock}), .sel(sel_I0), .en(enable));
  Decoder decoder_1 (.out0(decoder_1_out0), .out1(decoder_1_out1), .sel(write), .en(enable));
  and and_1 (and_1_out, reset, enable);
  or or_1 (or_1_out, demultiplexer_1_out0[1], and_1_out);
  or or_2 (or_2_out, demultiplexer_1_out1[1], and_1_out);
  or or_3 (or_3_out, demultiplexer_1_out2[1], and_1_out);
  or or_4 (or_4_out, demultiplexer_1_out3[1], and_1_out);
  or or_5 (or_5_out, demultiplexer_1_out4[1], and_1_out);
  or or_6 (or_6_out, demultiplexer_1_out5[1], and_1_out);
  or or_7 (or_7_out, demultiplexer_1_out6[1], and_1_out);
  or or_8 (or_8_out, demultiplexer_1_out7[1], and_1_out);
  Multiplexer #(.select(3), .width(8)) multiplexer_1 (
    .in0(register_8bit_1_outword), .in1(register_8bit_2_outword), .in2(register_8bit_3_outword),
    .in3(register_8bit_4_outword), .in4(register_8bit_5_outword), .in5(register_8bit_6_outword),
    .in6(register_8bit_7_outword), .in7(register_8bit_8_outword), .out(O0), .sel(sel_O0));
  REGISTER_8bit register_8bit_1 (
    .IE(decoder_1_out1), .clock(demultiplexer_1_out0[0]), .reset(or_1_out), .OE(decoder_1_out0), .InWord(I0),
    .OutWord(register_8bit_1_outword));
  REGISTER_8bit register_8bit_2 (
    .IE(decoder_1_out1), .clock(demultiplexer_1_out1[0]), .reset(or_2_out), .OE(decoder_1_out0), .InWord(I0),
    .OutWord(register_8bit_2_outword));
  REGISTER_8bit register_8bit_3 (
    .IE(decoder_1_out1), .clock(demultiplexer_1_out2[0]), .reset(or_3_out), .OE(decoder_1_out0), .InWord(I0),
    .OutWord(register_8bit_3_outword));
  REGISTER_8bit register_8bit_4 (
    .IE(decoder_1_out1), .clock(demultiplexer_1_out3[0]), .reset(or_4_out), .OE(decoder_1_out0), .InWord(I0),
    .OutWord(register_8bit_4_outword));
  REGISTER_8bit register_8bit_5 (
    .IE(decoder_1_out1), .clock(demultiplexer_1_out4[0]), .reset(or_5_out), .OE(decoder_1_out0), .InWord(I0),
    .OutWord(register_8bit_5_outword));
  REGISTER_8bit register_8bit_6 (
    .IE(decoder_1_out1), .clock(demultiplexer_1_out5[0]), .reset(or_6_out), .OE(decoder_1_out0), .InWord(I0),
    .OutWord(register_8bit_6_outword));
  REGISTER_8bit register_8bit_7 (
    .IE(decoder_1_out1), .clock(demultiplexer_1_out6[0]), .reset(or_7_out), .OE(decoder_1_out0), .InWord(I0),
    .OutWord(register_8bit_7_outword));
  REGISTER_8bit register_8bit_8 (
    .IE(decoder_1_out1), .clock(demultiplexer_1_out7[0]), .reset(or_8_out), .OE(decoder_1_out0), .InWord(I0),
    .OutWord(register_8bit_8_outword));
  Multiplexer #(.select(3), .width(8)) multiplexer_2 (
    .in0(register_8bit_1_outword), .in1(register_8bit_2_outword), .in2(register_8bit_3_outword),
    .in3(register_8bit_4_outword), .in4(register_8bit_5_outword), .in5(register_8bit_6_outword),
    .in6(register_8bit_7_outword), .in7(register_8bit_8_outword), .out(O1), .sel(sel_O1));

  // Notes on the sheet:
  //   General Inputs
  //   Register Specific
  //   Input Word
  //   Output Words
endmodule

module ALU_1bit (
  input  [1:0] op,
  input  Cin,
  input  A,
  input  B,
  output result,
  output over,
  output Cout
);

  wire and_1_out, and_2_out, AND_OP_out, FA_OP_0_out, FA_OP_1_out, or_1_out, OR_OP_out, xor_1_out;

  and and_1 (and_1_out, op[1], op[0]);
  or or_1 (or_1_out, and_1_out, Cin);
  xor xor_1 (xor_1_out, B, and_1_out);
  and AND_OP (AND_OP_out, A, xor_1_out);
  or OR_OP (OR_OP_out, A, xor_1_out);
  xor FA_OP_0 (FA_OP_0_out, A, xor_1_out);
  xor FA_OP_1 (FA_OP_1_out, or_1_out, FA_OP_0_out);
  and and_2 (and_2_out, or_1_out, FA_OP_0_out);
  Multiplexer #(.select(2)) multiplexer_1 (
    .in0(AND_OP_out), .in1(OR_OP_out), .in2(FA_OP_1_out), .in3(FA_OP_1_out), .out(result), .sel(op));
  or or_2 (Cout, and_2_out, AND_OP_out);
  xor xor_2 (over, or_1_out, Cout);

  // Notes on the sheet:
  //   AND: op=00, OR: op=01, ADD: op=10, SUB: op=11
endmodule

module ALU_8bit (
  input  [1:0] op,
  input  [7:0] A,
  input  [7:0] B,
  input  Cin,
  output [7:0] result,
  output zero,
  output neg,
  output over,
  output Cout
);

  wire alu_1bit_1_cout, alu_1bit_2_cout, alu_1bit_3_cout, alu_1bit_4_cout, alu_1bit_5_cout, alu_1bit_6_cout,
       alu_1bit_7_cout;

  ALU_1bit alu_1bit_1 (
    .op(op), .Cin(Cin), .A(A[0]), .B(B[0]), .result(result[0]), .Cout(alu_1bit_1_cout));  // open: over
  ALU_1bit alu_1bit_2 (
    .op(op), .Cin(alu_1bit_1_cout), .A(A[1]), .B(B[1]), .result(result[1]), .Cout(alu_1bit_2_cout));  // open: over
  ALU_1bit alu_1bit_3 (
    .op(op), .Cin(alu_1bit_2_cout), .A(A[2]), .B(B[2]), .result(result[2]), .Cout(alu_1bit_3_cout));  // open: over
  ALU_1bit alu_1bit_4 (
    .op(op), .Cin(alu_1bit_3_cout), .A(A[3]), .B(B[3]), .result(result[3]), .Cout(alu_1bit_4_cout));  // open: over
  ALU_1bit alu_1bit_5 (
    .op(op), .Cin(alu_1bit_4_cout), .A(A[4]), .B(B[4]), .result(result[4]), .Cout(alu_1bit_5_cout));  // open: over
  ALU_1bit alu_1bit_6 (
    .op(op), .Cin(alu_1bit_5_cout), .A(A[5]), .B(B[5]), .result(result[5]), .Cout(alu_1bit_6_cout));  // open: over
  ALU_1bit alu_1bit_7 (
    .op(op), .Cin(alu_1bit_6_cout), .A(A[6]), .B(B[6]), .result(result[6]), .Cout(alu_1bit_7_cout));  // open: over
  ALU_1bit alu_1bit_8 (.op(op), .Cin(alu_1bit_7_cout), .A(A[7]), .B(B[7]), .result(neg), .over(over), .Cout(Cout));
  nor nor_1 (zero, result[0], result[1], result[2], result[3], result[4], result[5], result[6], neg);

  assign result[7] = neg;
endmodule
