// Logisim project 00_first_logic_circuit.circ as structural Verilog: 2 circuits, main circuit main
module main (
  input  in_1,
  input  in_2,
  input  in_3,
  output out_4
);

  first_circuit first_circuit_1 (.X(in_1), .Y(in_2), .ENB(in_3), .Z(out_4));
endmodule

module first_circuit (
  input  X,
  input  Y,
  input  ENB,
  output Z
);

  wire and_1_out, and_2_out;

  and and_1 (and_1_out, X, ENB);
  and and_2 (and_2_out, Y, ENB);
  or or_1 (Z, and_1_out, and_2_out);
endmodule
