// Logisim project 01_first_exercises.circ as structural Verilog: 6 circuits, main circuit NOR_gate_using_AND
module NOR_gate_using_AND (
  input  in_1,
  input  in_2,
  output out_3
);

  and and_1 (out_3, ~in_1, ~in_2);  // AND_Gate

  // Notes on the sheet:
  //   NOR using AND
endmodule

module NOR_gate_using_OR (
  input  in_1,
  input  in_2,
  output out_3
);

  wire or_1_out;

  or or_1 (or_1_out, in_1, in_2);
  not not_1 (out_3, or_1_out);

  // Notes on the sheet:
  //   NOR using OR
endmodule

module XOR_gate_1 (
  input  in_1,
  input  in_2,
  output out_3
);

  wire and_1_out, and_2_out;

  and and_1 (and_1_out, ~in_1, in_2);  // AND_Gate
  and and_2 (and_2_out, in_1, ~in_2);  // AND_Gate
  or or_1 (out_3, and_1_out, and_2_out);

  // Notes on the sheet:
  //   A XOR B = A'B + AB'
endmodule

module XOR_gate_2 (
  input  in_1,
  input  in_2,
  output out_3
);

  wire or_1_out, or_2_out;

  or or_1 (or_1_out, in_1, in_2);
  or or_2 (or_2_out, ~in_1, ~in_2);  // OR_Gate
  and and_1 (out_3, or_1_out, or_2_out);

  // Notes on the sheet:
  //   A XOR B = (A + B)(A' + B')
endmodule

module rete_minimizzata (
  input  A,
  input  B,
  input  C,
  output out_4
);

  wire or_1_out;

  or or_1 (or_1_out, B, C);
  and and_1 (out_4, A, or_1_out);
endmodule

module rete_NON_minimizzata (
  input  A,
  input  B,
  input  C,
  output out_4
);

  wire ABC_out, and_1_out, and_2_out;

  and ABC (ABC_out, A, B, C);
  and and_1 (and_1_out, A, B, ~C);  // AND_Gate
  and and_2 (and_2_out, A, ~B, C);  // AND_Gate
  or or_1 (out_4, ABC_out, and_1_out, and_2_out);
endmodule
