// Logisim project 02_multiplexers.circ as structural Verilog: 8 circuits, main circuit MUX_2to1_1bit
module MUX_2to1_1bit (
  input  X0,
  input  X1,
  input  S,
  output O
);

  wire not_1_out, X0_0_out, X1_1_out;

  not not_1 (not_1_out, S);
  and X0_0 (X0_0_out, X0, not_1_out);
  and X1_1 (X1_1_out, X1, S);
  or or_1 (O, X0_0_out, X1_1_out);

  // Notes on the sheet:
  //   MUX 2to1_1bit
endmodule

module MUX_3to1_1bit (
  input  X0,
  input  X1,
  input  X2,
  input  [1:0] S,
  output O
);

  wire mux_2to1_1bit_1_o;

  MUX_2to1_1bit mux_2to1_1bit_1 (.X0(X0), .X1(X1), .S(S[0]), .O(mux_2to1_1bit_1_o));
  MUX_2to1_1bit mux_2to1_1bit_2 (.X0(mux_2to1_1bit_1_o), .X1(X2), .S(S[1]), .O(O));
endmodule

module MUX_4to1_1bit_raw (
  input  X0,
  input  X1,
  input  X2,
  input  X3,
  input  S1,
  input  S0,
  output O
);

  wire not_1_out, not_2_out, X0_00_out, X1_01_out, X2_10_out, X3_11_out;

  not not_1 (not_1_out, S1);
  not not_2 (not_2_out, S0);
  and X0_00 (X0_00_out, X0, not_1_out, not_2_out);
  and X1_01 (X1_01_out, X1, not_1_out, S0);
  and X2_10 (X2_10_out, X2, S1, not_2_out);
  and X3_11 (X3_11_out, X3, S1, S0);
  or or_1 (O, X0_00_out, X1_01_out, X2_10_out, X3_11_out);

  // Notes on the sheet:
  //   MUX 4to1_1bit
endmodule

module MUX_4to1_1bit (
  input  X0,
  input  X1,
  input  X2,
  input  X3,
  input  [1:0] S,
  output O
);

  wire mux_2to1_1bit_1_o, mux_2to1_1bit_2_o;

  MUX_2to1_1bit mux_2to1_1bit_1 (.X0(X0), .X1(X1), .S(S[0]), .O(mux_2to1_1bit_1_o));
  MUX_2to1_1bit mux_2to1_1bit_2 (.X0(X2), .X1(X3), .S(S[0]), .O(mux_2to1_1bit_2_o));
  MUX_2to1_1bit mux_2to1_1bit_3 (.X0(mux_2to1_1bit_1_o), .X1(mux_2to1_1bit_2_o), .S(S[1]), .O(O));

  // Notes on the sheet:
  //   MUX 4to1_1bit using 3x2to1_1bit
endmodule

module MUX_2to1_2bit (
  input  [1:0] X,
  input  [1:0] Y,
  input  S,
  output [1:0] O
);

  MUX_2to1_1bit mux_2to1_1bit_1 (.X0(X[0]), .X1(Y[0]), .S(S), .O(O[0]));
  MUX_2to1_1bit mux_2to1_1bit_2 (.X0(X[1]), .X1(Y[1]), .S(S), .O(O[1]));

  // Notes on the sheet:
  //   MUX 2to1_2bit using 2x2to1_1bit
endmodule

module MUX_2to1_4bit (
  input  [3:0] X,
  input  [3:0] Y,
  input  S,
  output [3:0] O
);

  MUX_2to1_2bit mux_2to1_2bit_1 (.X(X[1:0]), .Y(Y[1:0]), .S(S), .O(O[1:0]));
  MUX_2to1_2bit mux_2to1_2bit_2 (.X(X[3:2]), .Y(Y[3:2]), .S(S), .O(O[3:2]));

  // Notes on the sheet:
  //   MUX 2to1_4bit using 2x2to1_2bit
endmodule

module MUX_2to1_8bit (
  input  [7:0] X,
  input  [7:0] Y,
  input  S,
  output [7:0] O
);

  MUX_2to1_4bit mux_2to1_4bit_1 (.X(X[3:0]), .Y(Y[3:0]), .S(S), .O(O[3:0]));
  MUX_2to1_4bit mux_2to1_4bit_2 (.X(X[7:4]), .Y(Y[7:4]), .S(S), .O(O[7:4]));

  // Notes on the sheet:
  //   MUX 2to1_8bit using 2x2to1_4bit
endmodule

module MUX_4to1_8bit (
  input  [7:0] A,
  input  [7:0] B,
  input  [7:0] C,
  input  [7:0] D,
  input  [1:0] S,
  output [7:0] O
);

  wire [7:0] mux_2to1_8bit_1_o, mux_2to1_8bit_2_o;

  MUX_2to1_8bit mux_2to1_8bit_1 (.X(A), .Y(B), .S(S[0]), .O(mux_2to1_8bit_1_o));
  MUX_2to1_8bit mux_2to1_8bit_2 (.X(C), .Y(D), .S(S[0]), .O(mux_2to1_8bit_2_o));
  MUX_2to1_8bit mux_2to1_8bit_3 (.X(mux_2to1_8bit_1_o), .Y(mux_2to1_8bit_2_o), .S(S[1]), .O(O));

  // Notes on the sheet:
  //   MUX 4to1_8bit using 3x2to1_8bit
endmodule
