// Logisim project 03_demultiplexers.circ as structural Verilog: 5 circuits, main circuit DEMUX_1to2_1bit
module DEMUX_1to2_1bit (
  input  X,
  input  S,
  output Y0,
  output Y1
);

  and and_1 (Y0, X, ~S);  // AND_Gate
  and and_2 (Y1, X, S);
endmodule

module DEMUX_1to2_2bit (
  input  [1:0] X,
  input  S,
  output [1:0] Y0,
  output [1:0] Y1
);

  DEMUX_1to2_1bit demux_1to2_1bit_1 (.X(X[0]), .S(S), .Y0(Y0[0]), .Y1(Y1[0]));
  DEMUX_1to2_1bit demux_1to2_1bit_2 (.X(X[1]), .S(S), .Y0(Y0[1]), .Y1(Y1[1]));
endmodule

module DEMUX_1to2_4bit (
  input  [3:0] X,
  input  S,
  output [3:0] Y0,
  output [3:0] Y1
);

  DEMUX_1to2_2bit demux_1to2_2bit_1 (.X(X[1:0]), .S(S), .Y0(Y0[1:0]), .Y1(Y1[1:0]));
  DEMUX_1to2_2bit demux_1to2_2bit_2 (.X(X[3:2]), .S(S), .Y0(Y0[3:2]), .Y1(Y1[3:2]));
endmodule

module DEMUX_1to2_8bit (
  input  [7:0] X,
  input  S,
  output [7:0] Y0,
  output [7:0] Y1
);

  DEMUX_1to2_4bit demux_1to2_4bit_1 (.X(X[3:0]), .S(S), .Y0(Y0[3:0]), .Y1(Y1[3:0]));
  DEMUX_1to2_4bit demux_1to2_4bit_2 (.X(X[7:4]), .S(S), .Y0(Y0[7:4]), .Y1(Y1[7:4]));
endmodule

module DEMUX_1to4_8bit (
  input  [7:0] X,
  input  [1:0] S,
  output [7:0] Y0,
  output [7:0] Y1,
  output [7:0] Y2,
  output [7:0] Y3
);

  wire [7:0] demux_1to2_8bit_1_y0, demux_1to2_8bit_1_y1;

  DEMUX_1to2_8bit demux_1to2_8bit_1 (.X(X), .S(S[1]), .Y0(demux_1to2_8bit_1_y0), .Y1(demux_1to2_8bit_1_y1));
  DEMUX_1to2_8bit demux_1to2_8bit_2 (.X(demux_1to2_8bit_1_y0), .S(S[0]), .Y0(Y0), .Y1(Y1));
  DEMUX_1to2_8bit demux_1to2_8bit_3 (.X(demux_1to2_8bit_1_y1), .S(S[0]), .Y0(Y2), .Y1(Y3));
endmodule
