// Logisim project 05_memory_and_registers.circ as structural Verilog: 9 circuits, main circuit Latch_SR_OR
module Latch_SR_OR (
  input  reset,
  input  R,
  input  S,
  input  clock,
  output Q,
  output nQ
);

  wire and_1_out, and_2_out;

  and and_1 (and_1_out, R, clock);
  and and_2 (and_2_out, S, clock);
  nor nor_1 (Q, and_1_out, reset, nQ);
  nor nor_2 (nQ, Q, and_2_out);
endmodule

module Latch_D_OR (
  input  D,
  input  clock,
  input  reset,
  output Q,
  output nQ
);

  wire not_1_out;

  not not_1 (not_1_out, D);
  Latch_SR_OR latch_sr_or_1 (.R(D), .S(not_1_out), .clock(clock), .reset(reset), .Q(Q), .nQ(nQ));
endmodule

module FlipFlop_D_OR (
  input  D,
  input  clock,
  input  reset,
  output Q,
  output nQ
);

  wire latch_d_or_1_q, not_1_out;

  Latch_D_OR latch_d_or_1 (.D(D), .clock(not_1_out), .reset(reset), .Q(latch_d_or_1_q));  // open: nQ
  not not_1 (not_1_out, clock);
  Latch_D_OR latch_d_or_2 (.D(latch_d_or_1_q), .clock(clock), .reset(reset), .Q(Q), .nQ(nQ));
endmodule

module Latch_SR_NAND (
  input  R,
  input  S,
  input  reset,
  output Q,
  output nQ
);

  wire not_1_out;

  not not_1 (not_1_out, reset);
  nand nand_1 (Q, R, nQ);
  nand nand_2 (nQ, Q, not_1_out, S);
endmodule

module Latch_D_NAND (
  input  D,
  input  clock,
  input  reset,
  output Q,
  output nQ
);

  wire nand_1_out, nand_2_out;

  nand nand_1 (nand_1_out, D, clock);
  nand nand_2 (nand_2_out, nand_1_out, clock);
  Latch_SR_NAND latch_sr_nand_1 (.R(nand_1_out), .S(nand_2_out), .reset(reset), .Q(Q), .nQ(nQ));
endmodule

module FlipFlop_D_NAND (
  input  D,
  input  clock,
  input  reset,
  output Q,
  output nQ
);

  wire latch_d_nand_1_q, not_1_out;

  Latch_D_NAND latch_d_nand_1 (.D(D), .clock(not_1_out), .reset(reset), .Q(latch_d_nand_1_q));  // open: nQ
  not not_1 (not_1_out, clock);
  Latch_D_NAND latch_d_nand_2 (.D(latch_d_nand_1_q), .clock(clock), .reset(reset), .Q(Q), .nQ(nQ));
endmodule

module Register_1bit (
  input  D,
  input  enable,
  input  clock,
  input  reset,
  output Q,
  output nQ
);

  wire multiplexer_1_out;

  Multiplexer multiplexer_1 (.in0(Q), .in1(D), .out(multiplexer_1_out), .sel(enable));
  FlipFlop_D_OR flipflop_d_or_1 (.D(multiplexer_1_out), .clock(clock), .reset(reset), .Q(Q), .nQ(nQ));
endmodule

module Register_8bit (
  input  [7:0] InWord,
  input  IE,
  input  clock,
  input  reset,
  input  OE,
  output [7:0] OutWord
);

  wire register_1bit_1_q, register_1bit_2_q, register_1bit_3_q, register_1bit_4_q, register_1bit_5_q,
       register_1bit_6_q, register_1bit_7_q, register_1bit_8_q;

  Register_1bit register_1bit_1 (
    .D(InWord[7]), .enable(IE), .clock(clock), .reset(reset), .Q(register_1bit_1_q));  // open: nQ
  assign OutWord[7] = OE ? register_1bit_1_q : 1'bz;  // Controlled_Buffer controlled_buffer_1
  Register_1bit register_1bit_2 (
    .D(InWord[6]), .enable(IE), .clock(clock), .reset(reset), .Q(register_1bit_2_q));  // open: nQ
  assign OutWord[6] = OE ? register_1bit_2_q : 1'bz;  // Controlled_Buffer controlled_buffer_2
  Register_1bit register_1bit_3 (
    .D(InWord[5]), .enable(IE), .clock(clock), .reset(reset), .Q(register_1bit_3_q));  // open: nQ
  assign OutWord[5] = OE ? register_1bit_3_q : 1'bz;  // Controlled_Buffer controlled_buffer_3
  Register_1bit register_1bit_4 (
    .D(InWord[4]), .enable(IE), .clock(clock), .reset(reset), .Q(register_1bit_4_q));  // open: nQ
  assign OutWord[4] = OE ? register_1bit_4_q : 1'bz;  // Controlled_Buffer controlled_buffer_4
  Register_1bit register_1bit_5 (
    .D(InWord[3]), .enable(IE), .clock(clock), .reset(reset), .Q(register_1bit_5_q));  // open: nQ
  assign OutWord[3] = OE ? register_1bit_5_q : 1'bz;  // Controlled_Buffer controlled_buffer_5
  Register_1bit register_1bit_6 (
    .D(InWord[2]), .enable(IE), .clock(clock), .reset(reset), .Q(register_1bit_6_q));  // open: nQ
  assign OutWord[2] = OE ? register_1bit_6_q : 1'bz;  // Controlled_Buffer controlled_buffer_6
  Register_1bit register_1bit_7 (
    .D(InWord[1]), .enable(IE), .clock(clock), .reset(reset), .Q(register_1bit_7_q));  // open: nQ
  assign OutWord[1] = OE ? register_1bit_7_q : 1'bz;  // Controlled_Buffer controlled_buffer_7
  Register_1bit register_1bit_8 (
    .D(InWord[0]), .enable(IE), .clock(clock), .reset(reset), .Q(register_1bit_8_q));  // open: nQ
  assign OutWord[0] = OE ? register_1bit_8_q : 1'bz;  // Controlled_Buffer controlled_buffer_8
endmodule

module Memory_8x8bit (
  input  [2:0] sel_I0,
  input  [7:0] I0,
  input  [2:0] sel_O0,
  input  [2:0] sel_O1,
  input  enable,
  input  write,
  input  reset,
  input  clock,
  input  clear,
  output [7:0] O0,
  output [7:0] O1
);

  wire and_1_out, decoder_1_out0, decoder_1_out1, or_1_out, or_2_out, or_3_out, or_4_out, or_5_out, or_6_out,
       or_7_out, or_8_out;
  wire [1:0] demultiplexer_1_out0, demultiplexer_1_out1, demultiplexer_1_out2, demultiplexer_1_out3,
       demultiplexer_1_out4, demultiplexer_1_out5, demultiplexer_1_out6, demultiplexer_1_out7;
  wire [7:0] register_8bit_1_outword, register_8bit_2_outword, register_8bit_3_outword,
       register_8bit_4_outword, register_8bit_5_outword, register_8bit_6_outword, register_8bit_7_outword,
       register_8bit_8_outword;

  Demultiplexer #(.enable("true"), .select(3), .width(2)) demultiplexer_1 (
    .out0(demultiplexer_1_out0), .out1(demultiplexer_1_out1), .out2(demultiplexer_1_out2),
    .out3(demultiplexer_1_out3), .out4(demultiplexer_1_out4), .out5(demultiplexer_1_out5),
    .out6(demultiplexer_1_out6), .out7(demultiplexer_1_out7), .in({clear, clock}), .sel(sel_I0), .en(enable));
  and and_1 (and_1_out, reset, enable);
  Decoder decoder_1 (.out0(decoder_1_out0), .out1(decoder_1_out1), .sel(write), .en(enable));
  Register_8bit register_8bit_1 (
    .IE(decoder_1_out1), .clock(demultiplexer_1_out0[0]), .reset(or_1_out), .OE(decoder_1_out0), .InWord(I0),
    .OutWord(register_8bit_1_outword));
  or or_1 (or_1_out, demultiplexer_1_out0[1], and_1_out);
  Register_8bit register_8bit_2 (
    .IE(decoder_1_out1), .clock(demultiplexer_1_out1[0]), .reset(or_2_out), .OE(decoder_1_out0), .InWord(I0),
    .OutWord(register_8bit_2_outword));
  or or_2 (or_2_out, demultiplexer_1_out1[1], and_1_out);
  Register_8bit register_8bit_3 (
    .IE(decoder_1_out1), .clock(demultiplexer_1_out2[0]), .reset(or_3_out), .OE(decoder_1_out0), .InWord(I0),
    .OutWord(register_8bit_3_outword));
  or or_3 (or_3_out, demultiplexer_1_out2[1], and_1_out);
  Register_8bit register_8bit_4 (
    .IE(decoder_1_out1), .clock(demultiplexer_1_out3[0]), .reset(or_4_out), .OE(decoder_1_out0), .InWord(I0),
    .OutWord(register_8bit_4_outword));
  or or_4 (or_4_out, demultiplexer_1_out3[1], and_1_out);
  Register_8bit register_8bit_5 (
    .IE(decoder_1_out1), .clock(demultiplexer_1_out4[0]), .reset(or_5_out), .OE(decoder_1_out0), .InWord(I0),
    .OutWord(register_8bit_5_outword));
  or or_5 (or_5_out, demultiplexer_1_out4[1], and_1_out);
  Register_8bit register_8bit_6 (
    .IE(decoder_1_out1), .clock(demultiplexer_1_out5[0]), .reset(or_6_out), .OE(decoder_1_out0), .InWord(I0),
    .OutWord(register_8bit_6_outword));
  or or_6 (or_6_out, demultiplexer_1_out5[1], and_1_out);
  Register_8bit register_8bit_7 (
    .IE(decoder_1_out1), .clock(demultiplexer_1_out6[0]), .reset(or_7_out), .OE(decoder_1_out0), .InWord(I0),
    .OutWord(register_8bit_7_outword));
  or or_7 (or_7_out, demultiplexer_1_out6[1], and_1_out);
  Register_8bit register_8bit_8 (
    .IE(decoder_1_out1), .clock(demultiplexer_1_out7[0]), .reset(or_8_out), .OE(decoder_1_out0), .InWord(I0),
    .OutWord(register_8bit_8_outword));
  or or_8 (or_8_out, demultiplexer_1_out7[1], and_1_out);
  Multiplexer #(.select(3), .width(8)) multiplexer_1 (
    .in0(register_8bit_1_outword), .in1(register_8bit_2_outword), .in2(register_8bit_3_outword),
    .in3(register_8bit_4_outword), .in4(register_8bit_5_outword), .in5(register_8bit_6_outword),
    .in6(register_8bit_7_outword), .in7(register_8bit_8_outword), .out(O0), .sel(sel_O0));
  Multiplexer #(.select(3), .width(8)) multiplexer_2 (
    .in0(register_8bit_1_outword), .in1(register_8bit_2_outword), .in2(register_8bit_3_outword),
    .in3(register_8bit_4_outword), .in4(register_8bit_5_outword), .in5(register_8bit_6_outword),
    .in6(register_8bit_7_outword), .in7(register_8bit_8_outword), .out(O1), .sel(sel_O1));

  // Notes on the sheet:
  //   General Inputs
  //   Register Specific
  //   Input Word
  //   Output Words
endmodule
